# Fritzing sketch BatteryHarness (saved by Fritzing 0.8.0b)
stripboards: 5

parts:
  J1 = shrouded pin header, 10 pins [form="♂ (shrouded male)"]
  J2 = female pin header, 7 pins [form="♀ (female)"]
  J3 = female pin header, 7 pins [form="♀ (female)"]
  J4 = female pin header, 3 pins [form="♀ (female)"]
  U1 = Voltage Regulator - 5V [package="TO220 [THT]"]

nets:
  N1: J1.pin1, J2.pin5, J3.pin5, J4.pin2, U1.GND
  N2: J1.pin2, J2.pin6, J3.pin6, J4.pin3, U1.output_voltage
  N3: J1.pin3, J1.pin8
  N4: J1.pin4, J1.pin7
  N5: J1.pin5, J1.pin6
  N6: J2.pin2, J2.pin3
  N7: J2.pin7, J3.pin7, J4.pin1, U1.input_voltage
  N8: J3.pin2, J3.pin3
